# Fritzing sketch esquema papelera (saved by Fritzing 0.9.3b)
breadboards: 1

parts:
  Componente1 = Arduino Uno (Rev3)
  hc-sr1 = hc-sr04
  U1 = LCD-16X2 [package=lcd-8x2-kit]
  T1 = LM35 Temperature Sensor [package="TO92 [THT]"]
  J1 = Basic Servo
  R1 = Resistor [tolerance=±5% resistance=220 package=THT]
  R2 = Resistor [tolerance=±5% resistance=220 package=THT]

nets:
  N1: Componente1.A0, T1.Vout
  N2: Componente1.D8, hc-sr1.Trig
  N3: Componente1.D9_PWM, hc-sr1.Echo
  N4: Componente1.D11_PWM/MOSI, U1.E
  N5: Componente1.D12/MISO, U1.RS
  N6: Componente1.D13/SCK, J1.pulse
  GND: Componente1.GND, hc-sr1.GND, U1.VSS, U1.R_W, U1.K, T1.GND, J1.gnd, R2.Pin_0
  N7: Componente1.D2, U1.DB7
  N8: Componente1.D3_PWM, U1.DB6
  N9: Componente1.D4, U1.DB5
  N10: Componente1.D5_PWM, U1.DB4
  N11: Componente1.D6_PWM, U1.DB3
  N12: Componente1.D7, U1.DB2
  VCC: Componente1.5V, hc-sr1.VCC, U1.VDD, T1.+Vs, J1.vcc, R1.Pin_0
